# Fritzing sketch little_simon (saved by Fritzing 0.8.3b)
circuit board: 5.84cm x 5.84cm
breadboards: 1

parts:
  S4 = SWITCH-MOMENTARY-2 [package=tactile-pth-12mm]
  S1 = SWITCH-MOMENTARY-2 [package=tactile-pth-12mm]
  LED1 = LED - 5mm [color="Red (633nm)" package="5 mm [THT]"]
  LED2 = LED - 5mm [color="Blue (430nm)" package="5 mm [THT]"]
  LED3 = LED - 5mm [color="Yellow (595nm)" package="5 mm [THT]"]
  LED4 = LED - 5mm [color="Green (555nm)" package="5 mm [THT]"]
  U1 = IC, DIP package, 14 pins [chip_label=IC part_number=ATtiny44]
  SG1 = Buzzer 12mm [package=buzzer-12mm-ns]
  S5 = Toggle Switch [package=THT]
  R1 = Resistor [tolerance=±5% resistance=150 package=THT]
  R2 = Resistor [tolerance=±5% resistance=220 package=THT]
  R3 = Resistor [tolerance=±5% resistance=150 package=THT]
  R4 = Resistor [tolerance=±5% resistance=470 package=THT]
  R5 = Resistor [tolerance=±5% resistance=10k package=THT]
  C1 = Ceramic Capacitor [capacitance=100nF voltage=50V package="200 mil [THT, multilayer]"]
  C2 = Electrolytic Capacitor [capacitance=10µF voltage=35V package="100 mil [THT, electrolytic]"]
  S3 = SWITCH-MOMENTARY-2 [package=tactile-pth-12mm]
  S2 = SWITCH-MOMENTARY-2 [package=tactile-pth-12mm]
  BATT1 = 3xAAA Switchable Battery Pack w/Bare Wire

nets:
  N1: S4.1, S1.2, LED1.cathode, LED2.cathode, LED3.cathode, LED4.cathode, U1.pin14, SG1.2, C1.0, C2.-, S3.2, S2.1, BATT1.NEG
  N2: S4.2, U1.pin2
  N3: S1.1, U1.pin6
  N4: LED1.anode, R1.Pin_1
  N5: LED2.anode, R2.Pin_1
  N6: LED3.anode, R3.Pin_1
  N7: LED4.anode, R4.Pin_1
  N8: U1.pin1, S5.L2, R5.Pin_1, C1.1, C2.+
  N9: U1.pin3, S3.1
  N10: U1.pin4, R5.Pin_0
  N11: U1.pin5, S2.2
  N12: U1.pin8, SG1.1
  N13: U1.pin9, R4.Pin_0
  N14: U1.pin10, R3.Pin_0
  N15: U1.pin11, R2.Pin_0
  N16: U1.pin12, R1.Pin_0
  N17: S5.L1, S5.COM, BATT1.POS

notes:
  little_simon
  by peter (2013)
  sites.google.com/site/creationsbypeter
  on
  off
  R
  B
  Y
  G
  +
  -

custom parts:
  3xAAA Switchable Battery Pack w/Bare Wire: 3xAAA Switchable Battery Pack w/Bare Wire Connectors
